// Logisim project MemoryHandshakes.circ as structural Verilog: 1 circuit, main circuit main
module main (
  input  in_1,
  input  in_2,
  input  in_3,
  input  WriteEn,
  input  in_5,
  input  in_6,
  input  in_7,
  output Stall,
  output out_9,
  output out_10,
  output out_11,
  output out_12
);

  wire and_1_out, and_2_out, and_3_out, and_4_out;

  or or_1 (Stall, and_2_out, and_1_out);
  and and_1 (and_1_out, in_5, ~in_3);  // AND_Gate
  and and_2 (and_2_out, in_7, ~in_6);  // AND_Gate
  or or_2 (out_9, and_3_out, and_4_out);
  and and_3 (and_3_out, in_1, ~WriteEn);  // AND_Gate
  and and_4 (and_4_out, in_2, WriteEn);
  RAM #(.databus("bibus")) ram_1 (.we(and_4_out));  // open: addr, oe, clk, din, dout
  and and_5 (out_10, ~WriteEn, in_2);  // AND_Gate

  assign out_11 = in_5;
  assign out_12 = in_7;
endmodule
